# Fritzing sketch BreadBoardArduino (saved by Fritzing 0.7.1b)
breadboards: 1

parts:
  U1 = atmega328 [package=dip]
  Y1 = Resonator [frequency="16 Mhz" package=THT]
  LED1 = LED - 5mm [color="Green (555nm)" part_number="Power Indicator" package="5 mm [THT]"]
  R1 = Resistor [tolerance=±5% resistance=220 package=THT]
  J1 = Screw terminal - 2 pins [package=THT]
  U2 = Voltage Regulator - 5V [package="TO220 [THT]"]
  C1 = Electrolytic Capacitor [capacitance=10µF package="100 mil [THT, electrolytic]"]
  C2 = Electrolytic Capacitor [capacitance=1µF package="100 mil [THT, electrolytic]"]
  S1 = Pushbutton [package="[THT]"]
  R2 = Resistor [tolerance=±5% resistance=10k package=THT]
  LED2 = LED - 5mm [color="Yellow (585nm)" package="5 mm [THT]"]
  R3 = Resistor [tolerance=±5% resistance=220 package=THT]
  C3 = Ceramic Capacitor [capacitance=100nF package="100 mil [THT, multilayer]"]
  IC1 = IC, DIP package, 10 pins [chip_label="USB Serial" spacing=600mil]

nets:
  N1: U1.RESET, S1.Pin_1, S1.Pin_2, R2.Pin_0, C3.1
  N2: U1.D0_(RX), IC1.pin9
  N3: U1.D1_(TX), IC1.pin8
  N4: U1.VCC, R1.Pin_1, R2.Pin_1
  N5: U1.GND#7, LED1.cathode, S1.Pin_3, S1.Pin_4
  N6: U1.XLAT1, Y1.0
  N7: U1.XLAT2, Y1.pin_1
  N8: U1.D13, LED2.anode
  N9: U1.AVCC, U1.AREF, U2.output_voltage, C1.+
  N10: U1.GND#21, J1.pin2, U2.GND, C1.-, C2.-
  N11: Y1.GND, R3.Pin_0, IC1.pin3
  N12: LED1.anode, R1.Pin_0
  N13: J1.pin1, U2.input_voltage, C2.+
  N14: LED2.cathode, R3.Pin_1
  N15: C3.0, IC1.pin5

notes:
  Plans called for 220ohm resisters on the LEDs. I used 330s because that's what I had.
