# Fritzing sketch ClockDisplay (saved by Fritzing 0.7.1b)
breadboards: 2

parts:
  DispH1 = 7-Segment LED Display [package=THT]
  DispH2 = 7-Segment LED Display [package=THT]
  DispM1 = 7-Segment LED Display [package=THT]
  DispM2 = 7-Segment LED Display [package=THT]
  LED1 = LED - 3mm [color="Red (633nm)" package="3 mm [THT]"]
  LED2 = LED - 3mm [color="Red (633nm)" package="3 mm [THT]"]
  Arduino1 = Arduino
  R1 = Resistor [tolerance=±5% resistance=2.2k package=THT]
  R2 = Resistor [tolerance=±5% resistance=2.2k package=THT]
  R3 = Resistor [tolerance=±5% resistance=10k package=THT]
  IC3 = IC, DIP package, 28 pins [chip_label="TLC 5940" spacing=300mil]
  IC4 = IC, DIP package, 28 pins [chip_label="TLC 5940" spacing=300mil]
  Part1 = Real Time Clock Module - DS1307 RTC Breakout Board
  U1 = Voltage Regulator - 5V [package="TO220 [THT]"]
  VCC1 = Battery block 9V

nets:
  N1: DispH1.cathodeE, IC4.pin4
  N2: DispH1.cathodeD, IC4.pin3
  N3: DispH1.cathodeC, IC4.pin2
  N4: DispH1.cathodeDP, IC4.pin7
  N5: DispH1.cathodeB, IC4.pin1
  N6: DispH1.cathodeA, IC4.pin28
  N7: DispH1.cathodeF, IC4.pin5
  N8: DispH1.cathodeG, IC4.pin6
  N9: DispH2.cathodeE, IC4.pin12
  N10: DispH2.cathodeD, IC4.pin11
  N11: DispH2.cathodeC, IC4.pin10
  N12: DispH2.cathodeDP, IC4.pin15
  N13: DispH2.cathodeB, IC4.pin9
  N14: DispH2.cathodeA, IC4.pin8
  N15: DispH2.cathodeF, IC4.pin13
  N16: DispH2.cathodeG, IC4.pin14
  N17: DispM1.cathodeE, IC3.pin4
  N18: DispM1.cathodeD, IC3.pin3
  N19: DispM1.cathodeC, IC3.pin2
  N20: DispM1.cathodeDP, IC3.pin7
  N21: DispM1.cathodeB, IC3.pin1
  N22: DispM1.cathodeA, IC3.pin28
  N23: DispM1.cathodeF, IC3.pin5
  N24: DispM1.cathodeG, IC3.pin6
  N25: DispM2.cathodeE, IC3.pin12
  N26: DispM2.cathodeD, IC3.pin11
  N27: DispM2.cathodeC, IC3.pin10
  N28: DispM2.cathodeB, IC3.pin9
  N29: DispM2.cathodeA, IC3.pin8
  N30: DispM2.cathodeF, IC3.pin13
  N31: DispM2.cathodeG, IC3.pin14
  N32: LED1.cathode, IC3.pin15
  N33: LED1.anode, LED2.anode
  N34: LED2.cathode, Arduino1.+5V, R3.Pin_0, IC4.pin19, IC4.pin21
  N35: Arduino1.GND, R2.Pin_0, IC4.pin22, IC4.pin27
  N36: Arduino1.D13, IC3.pin25, IC4.pin25
  N37: Arduino1.D11, IC4.pin26
  N38: Arduino1.D10, R3.Pin_1, IC3.pin23, IC4.pin23
  N39: Arduino1.D9, IC3.pin24, IC4.pin24
  N40: Arduino1.D3, IC3.pin18, IC4.pin18
  N41: Arduino1.A4, Part1.SDA
  N42: Arduino1.A5, Part1.SCL
  GND: R1.Pin_0, IC3.pin22, IC3.pin27, Part1.GND, U1.GND, VCC1.-
  N43: R1.Pin_1, IC3.pin20
  N44: R2.Pin_1, IC4.pin20
  N45: IC3.pin19, IC3.pin21
  N46: IC3.pin26, IC4.pin17
  N47: Part1.5V, U1.output_voltage
  N48: U1.input_voltage, VCC1.+

notes:
  8 segment
  led pins:
  A - 7 (blue)
  B - 6 (yellow)
  C - 4 (green)
  D - 2 (grey)
  E - 1 (white)
  F - 9 (orange)
  G - 10 (brown)
  DP - 5 (purple)
  We do not hook up the decimal place (DP) for the final digit. Instead, we use the signal that would have been connected to it to control the two LEDs in the middle that are the colon for time mode display. This lets us use the display for fractional numbers, such as the temperature ("68.5F" for example)
  When the LED display is too bright, it draws too much current and the RTC module stops working.
  My solution is to add a separate 5V power supply for the RTC module.
  For the final version I'll want a transister in there somewhere, so I can control the power supply from the arduino.
  Using the second power supply to drive the LED display doesn't work. My theory is that it is because the data pins are drawing power from the arduino and so need to be on the same Vcc.
