# Fritzing sketch PowerSupply (saved by Fritzing 0.7.1b)
perfboards: 1

parts:
  S1 = Toggle Switch [package=THT]  # not connected
  J1 = female pin header, 2 pins [form="♀ (female)"]
  J2 = female pin header, 2 pins [form="♀ (female)"]
  D1 = Rectifier Diode [part_number=1N4001 package="300 mil [THT]"]
  D2 = Rectifier Diode [part_number=1N4001 package="300 mil [THT]"]
  J3 = female pin header, 3 pins [form="♀ (female)"]
  U1 = mystery part, 2 pins [chip_label="Resettable fuse PTC" spacing=300mil]
  U3 = Voltage Regulator - 5V [package="TO220 [THT]"]  # not connected
  U5 = Voltage Regulator - 5V [package="TO220 [THT]"]  # not connected
  C1 = Electrolytic Capacitor [capacitance=0.1mF package="100 mil [THT, electrolytic]"]  # not connected
  C2 = Electrolytic Capacitor [capacitance=10µF package="100 mil [THT, electrolytic]"]
  U6 = Voltage Regulator - 3.3V [package="TO220 [THT]"]  # not connected
  C3 = Electrolytic Capacitor [capacitance=0.1mF package="100 mil [THT, electrolytic]"]  # not connected
  C4 = Electrolytic Capacitor [capacitance=1µF package="100 mil [THT, electrolytic]"]  # not connected

nets:
  N1: J1.pin1, J2.pin1, C2.-
  N2: J1.pin2, D1.anode
  N3: J2.pin2, D2.anode
  N4: D1.cathode, J3.pin3
  N5: D2.cathode, J3.pin1
  N6: J3.pin2, U1.pin1

custom parts:
  Voltage Regulator - 5V: 3.3V DC Voltage Regulator
